// Logisim project new chess clock timer.circ as structural Verilog: 6 circuits, main circuit Chess Digital Clock
module Chess_Digital_Clock (
  input  _0_STOP___1_START,
  input  surrender,
  input  surrender_2,
  input  _0_BOB___1_ALICE
);

  wire ALICE_out_3, ALICE_out_4, ALICE_out_5, ALICE_out_6, ALICE_out_7, ALICE_out_8, ALICE_out_9,
       ALICE_out_10, ALICE_out_11, ALICE_out_12, ALICE_out_13, ALICE_out_14, ALICE_out_15, ALICE_out_16,
       ALICE_out_17, ALICE_out_18, ALICE_out_19, ALICE_out_20, ALICE_out_21, ALICE_out_22, ALICE_out_23,
       ALICE_out_24, ALICE_out_25, ALICE_out_26, ALICE_out_27, ALICE_out_28, ALICE_out_29, ALICE_out_30,
       and_1_out, and_2_out, and_3_out, BOB_out_3, BOB_out_4, BOB_out_5, BOB_out_6, BOB_out_7, BOB_out_8,
       BOB_out_9, BOB_out_10, BOB_out_11, BOB_out_12, BOB_out_13, BOB_out_14, BOB_out_15, BOB_out_16,
       BOB_out_17, BOB_out_18, BOB_out_19, BOB_out_20, BOB_out_21, BOB_out_22, BOB_out_23, BOB_out_24,
       BOB_out_25, BOB_out_26, BOB_out_27, BOB_out_28, BOB_out_29, BOB_out_30, clock_1_out, not_1_out,
       not_2_out, not_3_out, or_1_out, RESET_out;

  LED led_1 (.in(surrender));
  LED led_2 (.in(surrender_2));
  Button RESET (.out(RESET_out));
  Clock clock_1 (.out(clock_1_out));
  _7_Segment_Display u_7_segment_display_1 (
    .g(ALICE_out_8), .f(ALICE_out_10), .a(ALICE_out_16), .b(ALICE_out_15), .e(ALICE_out_12),
    .d(ALICE_out_13), .c(ALICE_out_14), .dp(and_1_out));
  _7_Segment_Display u_7_segment_display_2 (
    .g(ALICE_out_18), .f(ALICE_out_20), .a(ALICE_out_30), .b(ALICE_out_28), .e(ALICE_out_22),
    .d(ALICE_out_24), .c(ALICE_out_26));  // open: dp
  not not_1 (not_1_out, _0_STOP___1_START);
  _7_Segment_Display u_7_segment_display_3 (
    .g(ALICE_out_17), .f(ALICE_out_19), .a(ALICE_out_29), .b(ALICE_out_27), .e(ALICE_out_21),
    .d(ALICE_out_23), .c(ALICE_out_25));  // open: dp
  or or_1 (or_1_out, surrender, not_1_out, surrender_2);
  not not_2 (not_2_out, _0_BOB___1_ALICE);
  and and_1 (and_1_out, not_2_out, and_2_out);
  xx_xx ALICE (
    .out_3(ALICE_out_3), .out_4(ALICE_out_4), .out_5(ALICE_out_5), .out_6(ALICE_out_6), .out_7(ALICE_out_7),
    .out_9(ALICE_out_9), .out_11(ALICE_out_11), .out_17(ALICE_out_17), .out_19(ALICE_out_19),
    .out_21(ALICE_out_21), .out_23(ALICE_out_23), .out_25(ALICE_out_25), .out_27(ALICE_out_27),
    .out_29(ALICE_out_29), .out_8(ALICE_out_8), .out_10(ALICE_out_10), .out_12(ALICE_out_12),
    .out_13(ALICE_out_13), .out_14(ALICE_out_14), .out_15(ALICE_out_15), .out_16(ALICE_out_16),
    .out_18(ALICE_out_18), .out_20(ALICE_out_20), .out_22(ALICE_out_22), .out_24(ALICE_out_24),
    .out_26(ALICE_out_26), .out_28(ALICE_out_28), .out_30(ALICE_out_30), ._0(RESET_out), .in_1(and_1_out));
  _7_Segment_Display u_7_segment_display_4 (
    .g(ALICE_out_3), .f(ALICE_out_4), .a(ALICE_out_11), .b(ALICE_out_9), .e(ALICE_out_5), .d(ALICE_out_6),
    .c(ALICE_out_7));  // open: dp
  not not_3 (not_3_out, or_1_out);
  and and_2 (and_2_out, not_3_out, clock_1_out);
  _7_Segment_Display u_7_segment_display_5 (
    .g(BOB_out_18), .f(BOB_out_20), .a(BOB_out_30), .b(BOB_out_28), .e(BOB_out_22), .d(BOB_out_24),
    .c(BOB_out_26));  // open: dp
  _7_Segment_Display u_7_segment_display_6 (
    .g(BOB_out_17), .f(BOB_out_19), .a(BOB_out_29), .b(BOB_out_27), .e(BOB_out_21), .d(BOB_out_23),
    .c(BOB_out_25));  // open: dp
  _7_Segment_Display u_7_segment_display_7 (
    .g(BOB_out_8), .f(BOB_out_10), .a(BOB_out_16), .b(BOB_out_15), .e(BOB_out_12), .d(BOB_out_13),
    .c(BOB_out_14), .dp(and_3_out));
  _7_Segment_Display u_7_segment_display_8 (
    .g(BOB_out_3), .f(BOB_out_4), .a(BOB_out_11), .b(BOB_out_9), .e(BOB_out_5), .d(BOB_out_6), .c(BOB_out_7));  // open: dp
  and and_3 (and_3_out, and_2_out, _0_BOB___1_ALICE);
  LED led_3 (.in(surrender_2));
  LED led_4 (.in(surrender));
  xx_xx BOB (
    .out_3(BOB_out_3), .out_4(BOB_out_4), .out_5(BOB_out_5), .out_6(BOB_out_6), .out_7(BOB_out_7),
    .out_9(BOB_out_9), .out_11(BOB_out_11), .out_17(BOB_out_17), .out_19(BOB_out_19), .out_21(BOB_out_21),
    .out_23(BOB_out_23), .out_25(BOB_out_25), .out_27(BOB_out_27), .out_29(BOB_out_29), .out_8(BOB_out_8),
    .out_10(BOB_out_10), .out_12(BOB_out_12), .out_13(BOB_out_13), .out_14(BOB_out_14), .out_15(BOB_out_15),
    .out_16(BOB_out_16), .out_18(BOB_out_18), .out_20(BOB_out_20), .out_22(BOB_out_22), .out_24(BOB_out_24),
    .out_26(BOB_out_26), .out_28(BOB_out_28), .out_30(BOB_out_30), ._0(RESET_out), .in_1(and_3_out));
endmodule

module xx_xx (
  input  in_1,
  input  _0,
  output out_3,
  output out_4,
  output out_5,
  output out_6,
  output out_7,
  output out_8,
  output out_9,
  output out_10,
  output out_11,
  output out_12,
  output out_13,
  output out_14,
  output out_15,
  output out_16,
  output out_17,
  output out_18,
  output out_19,
  output out_20,
  output out_21,
  output out_22,
  output out_23,
  output out_24,
  output out_25,
  output out_26,
  output out_27,
  output out_28,
  output out_29,
  output out_30
);

  wire and_1_out, and_2_out, and_3_out;
  wire [3:0] counter_1_q, counter_2_q, counter_3_q, counter_4_q;

  Counter #(.width(4), .max('h9)) counter_1 (
    .load(1'b1), .Q(counter_1_q), .clk(in_1), .clr(_0));  // open: D, count, carry
  Counter #(.width(4), .max('h5)) counter_2 (
    .load(1'b1), .Q(counter_2_q), .clk(and_1_out), .clr(_0));  // open: D, count, carry
  and and_1 (and_1_out, counter_1_q[3], counter_1_q[0], ~counter_1_q[2], ~counter_1_q[1]);  // AND_Gate
  x__7_segDisplay x_7_segdisplay_1 (
    .s03(counter_1_q[3]), .s02(counter_1_q[2]), .s01(counter_1_q[1]), .s00(counter_1_q[0]), .g(out_3),
    .f(out_4), .e(out_5), .d(out_6), .c(out_7), .b(out_9), .a(out_11));
  x__7_segDisplay_2 x_7_segdisplay_2 (
    .s02(counter_2_q[2]), .s01(counter_2_q[1]), .s00(counter_2_q[0]), .g(out_17), .f(out_19), .e(out_21),
    .d(out_23), .c(out_25), .b(out_27), .a(out_29));
  and and_2 (and_2_out, ~counter_2_q[3], counter_2_q[2], ~counter_2_q[1], counter_2_q[0]);  // AND_Gate
  Counter #(.width(4), .max('h4)) counter_3 (
    .load(1'b1), .Q(counter_3_q), .clk(and_2_out), .clr(_0));  // open: D, count, carry
  Counter #(.width(4), .max('h0)) counter_4 (
    .load(1'b1), .Q(counter_4_q), .clk(and_3_out), .clr(_0));  // open: D, count, carry
  and and_3 (and_3_out, counter_3_q[0], ~counter_3_q[1], ~counter_3_q[2], counter_3_q[3]);  // AND_Gate
  x____7_segDisplay x_7_segdisplay_3 (
    .s03(counter_3_q[3]), .s02(counter_3_q[2]), .s01(counter_3_q[1]), .s00(counter_3_q[0]), .g(out_8),
    .f(out_10), .e(out_12), .d(out_13), .c(out_14), .b(out_15), .a(out_16));
  x_____7_segDisplay x_7_segdisplay_4 (
    .s02(counter_4_q[2]), .s01(counter_4_q[1]), .s00(counter_4_q[0]), .g(out_18), .f(out_20), .e(out_22),
    .d(out_24), .c(out_26), .b(out_28), .a(out_30));
endmodule

// --:-x
module x__7_segDisplay (
  input  s03,
  input  s02,
  input  s01,
  input  s00,
  output g,
  output f,
  output e,
  output d,
  output c,
  output b,
  output a
);

  wire and_1_out, and_2_out, and_3_out, and_4_out, and_5_out, and_6_out, and_7_out, and_8_out, and_9_out,
       and_10_out, and_11_out, and_12_out, and_13_out, and_14_out, and_15_out, and_16_out, and_17_out,
       and_18_out, and_19_out, and_20_out, and_21_out, and_22_out, and_23_out, and_24_out, and_25_out,
       and_26_out, and_27_out, not_1_out, not_2_out, not_3_out, not_4_out, not_5_out, not_6_out, not_7_out,
       not_8_out, not_9_out, not_10_out, not_11_out, not_12_out, not_13_out, not_14_out, not_15_out,
       not_16_out, not_17_out, not_18_out, not_19_out, not_20_out, not_21_out, not_22_out, not_23_out,
       not_24_out, not_25_out, not_26_out, not_27_out, not_28_out, not_29_out, not_30_out, not_31_out,
       not_32_out, not_33_out, not_34_out, not_35_out, not_36_out, not_37_out, not_38_out, not_39_out,
       not_40_out, not_41_out, not_42_out;

  not not_1 (not_1_out, s03);
  and and_1 (and_1_out, not_1_out, not_2_out, s01);
  not not_2 (not_2_out, s02);
  and and_2 (and_2_out, s01, not_3_out);
  not not_3 (not_3_out, s00);
  and and_3 (and_3_out, s02, not_4_out);
  not not_4 (not_4_out, s01);
  and and_4 (and_4_out, s03, not_5_out);
  not not_5 (not_5_out, s01);
  and and_5 (and_5_out, s03, s02);
  not not_6 (not_6_out, s03);
  and and_6 (and_6_out, not_6_out, not_7_out, not_8_out);
  not not_7 (not_7_out, s01);
  not not_8 (not_8_out, s00);
  not not_9 (not_9_out, s03);
  and and_7 (and_7_out, not_9_out, s02, not_10_out);
  not not_10 (not_10_out, s01);
  not not_11 (not_11_out, s03);
  and and_8 (and_8_out, not_11_out, s02, not_12_out);
  not not_12 (not_12_out, s00);
  and and_9 (and_9_out, s03, not_13_out, not_14_out);
  not not_13 (not_13_out, s02);
  not not_14 (not_14_out, s01);
  not not_15 (not_15_out, s02);
  and and_10 (and_10_out, not_15_out, not_16_out);
  not not_16 (not_16_out, s00);
  not not_17 (not_17_out, s03);
  and and_11 (and_11_out, not_17_out, s01, not_18_out);
  not not_18 (not_18_out, s00);
  not not_19 (not_19_out, s01);
  and and_12 (and_12_out, s03, not_19_out, not_20_out);
  not not_20 (not_20_out, s00);
  not not_21 (not_21_out, s02);
  and and_13 (and_13_out, not_21_out, not_22_out);
  not not_22 (not_22_out, s00);
  not not_23 (not_23_out, s03);
  not not_24 (not_24_out, s02);
  and and_14 (and_14_out, not_23_out, not_24_out, s01);
  not not_25 (not_25_out, s03);
  and and_15 (and_15_out, not_25_out, s01, not_26_out);
  not not_26 (not_26_out, s00);
  and and_16 (and_16_out, s02, not_27_out, s00);
  not not_27 (not_27_out, s01);
  and and_17 (and_17_out, s03, not_28_out, not_29_out);
  not not_28 (not_28_out, s02);
  not not_29 (not_29_out, s01);
  and and_18 (and_18_out, s03, s02, s00);
  not not_30 (not_30_out, s02);
  and and_19 (and_19_out, not_30_out, not_31_out);
  not not_31 (not_31_out, s01);
  not not_32 (not_32_out, s03);
  and and_20 (and_20_out, not_32_out, s02);
  not not_33 (not_33_out, s03);
  and and_21 (and_21_out, not_33_out, not_34_out, not_35_out);
  not not_34 (not_34_out, s01);
  not not_35 (not_35_out, s00);
  not not_36 (not_36_out, s02);
  and and_22 (and_22_out, s01, s00);
  and and_23 (and_23_out, s03, s01);
  not not_37 (not_37_out, s02);
  and and_24 (and_24_out, not_37_out, not_38_out);
  not not_38 (not_38_out, s00);
  not not_39 (not_39_out, s03);
  and and_25 (and_25_out, not_39_out, s01);
  not not_40 (not_40_out, s03);
  and and_26 (and_26_out, not_40_out, s02, s00);
  not not_41 (not_41_out, s02);
  and and_27 (and_27_out, s03, not_41_out, not_42_out);
  not not_42 (not_42_out, s01);
  or or_1 (g, and_1_out, and_2_out, and_3_out, and_4_out, and_5_out);
  or or_2 (f, and_6_out, and_7_out, and_8_out, and_9_out);
  or or_3 (e, and_10_out, and_11_out, and_12_out);
  or or_4 (c, and_19_out, s00, and_20_out);
  or or_5 (b, and_21_out, not_36_out, and_22_out, and_23_out);
  or or_6 (a, and_24_out, and_25_out, and_26_out, and_27_out);
  or or_7 (d, and_13_out, and_14_out, and_15_out, and_16_out, and_17_out, and_18_out);
endmodule

// --:x-
module x__7_segDisplay_2 (
  input  s02,
  input  s01,
  input  s00,
  output g,
  output f,
  output e,
  output d,
  output c,
  output b,
  output a
);

  wire and_1_out, and_2_out, and_4_out, and_5_out, and_6_out, and_7_out, and_8_out, and_9_out, not_1_out,
       not_2_out, not_3_out, not_4_out, not_5_out, not_6_out, not_7_out, not_8_out, not_9_out, not_10_out,
       not_11_out, not_12_out, not_13_out, not_14_out, not_15_out, not_16_out;

  or or_1 (g, s01, s02);
  not not_1 (not_1_out, s01);
  not not_2 (not_2_out, s00);
  not not_3 (not_3_out, s01);
  not not_4 (not_4_out, s02);
  not not_5 (not_5_out, s00);
  not not_6 (not_6_out, s02);
  not not_7 (not_7_out, s00);
  not not_8 (not_8_out, s02);
  not not_9 (not_9_out, s01);
  not not_10 (not_10_out, s01);
  not not_11 (not_11_out, s02);
  not not_12 (not_12_out, s00);
  not not_13 (not_13_out, s02);
  not not_14 (not_14_out, s00);
  not not_15 (not_15_out, s02);
  not not_16 (not_16_out, s01);
  and and_1 (and_1_out, not_1_out, not_2_out);
  and and_2 (and_2_out, s02, not_3_out);
  and and_3 (e, not_4_out, not_5_out);
  and and_4 (and_4_out, not_6_out, not_7_out);
  and and_5 (and_5_out, not_8_out, s01);
  and and_6 (and_6_out, s02, not_9_out, s00);
  or or_2 (c, not_10_out, s00);
  or or_3 (b, not_11_out, not_12_out, s01);
  and and_7 (and_7_out, not_13_out, not_14_out);
  and and_8 (and_8_out, not_15_out, s01);
  and and_9 (and_9_out, s02, not_16_out, s00);
  or or_4 (f, and_1_out, and_2_out);
  or or_5 (d, and_4_out, and_5_out, and_6_out);
  or or_6 (a, and_7_out, and_8_out, and_9_out);
endmodule

// -x:--
module x____7_segDisplay (
  input  s03,
  input  s02,
  input  s01,
  input  s00,
  output g,
  output f,
  output e,
  output d,
  output c,
  output b,
  output a
);

  wire and_1_out, and_2_out, and_3_out, and_4_out, and_5_out, and_6_out, and_7_out, and_8_out, and_9_out,
       and_10_out, and_11_out, and_12_out, and_13_out, and_14_out, and_15_out, and_16_out, and_17_out,
       and_18_out, and_19_out, and_20_out, and_21_out, and_22_out, and_23_out, and_24_out, and_25_out,
       and_26_out, and_27_out, not_1_out, not_2_out, not_3_out, not_4_out, not_5_out, not_6_out, not_7_out,
       not_8_out, not_9_out, not_10_out, not_11_out, not_12_out, not_13_out, not_14_out, not_15_out,
       not_16_out, not_17_out, not_18_out, not_19_out, not_20_out, not_21_out, not_22_out, not_23_out,
       not_24_out, not_25_out, not_26_out, not_27_out, not_28_out, not_29_out, not_30_out, not_31_out,
       not_32_out, not_33_out, not_34_out, not_35_out, not_36_out, not_37_out, not_38_out, not_39_out,
       not_40_out, not_41_out, not_42_out;

  not not_1 (not_1_out, s03);
  not not_2 (not_2_out, s02);
  and and_1 (and_1_out, not_1_out, not_2_out, s01);
  and and_2 (and_2_out, s01, not_3_out);
  not not_3 (not_3_out, s00);
  and and_3 (and_3_out, s02, not_4_out);
  not not_4 (not_4_out, s01);
  and and_4 (and_4_out, s03, not_5_out);
  not not_5 (not_5_out, s01);
  and and_5 (and_5_out, s03, s02);
  not not_6 (not_6_out, s03);
  not not_7 (not_7_out, s01);
  and and_6 (and_6_out, not_6_out, not_7_out, not_8_out);
  not not_8 (not_8_out, s00);
  not not_9 (not_9_out, s03);
  and and_7 (and_7_out, not_9_out, s02, not_10_out);
  not not_10 (not_10_out, s01);
  not not_11 (not_11_out, s03);
  and and_8 (and_8_out, not_11_out, s02, not_12_out);
  not not_12 (not_12_out, s00);
  not not_13 (not_13_out, s02);
  and and_9 (and_9_out, s03, not_13_out, not_14_out);
  not not_14 (not_14_out, s01);
  not not_15 (not_15_out, s02);
  and and_10 (and_10_out, not_15_out, not_16_out);
  not not_16 (not_16_out, s00);
  not not_17 (not_17_out, s03);
  and and_11 (and_11_out, not_17_out, s01, not_18_out);
  not not_18 (not_18_out, s00);
  and and_12 (and_12_out, s03, not_19_out, not_20_out);
  not not_19 (not_19_out, s01);
  not not_20 (not_20_out, s00);
  not not_21 (not_21_out, s02);
  and and_13 (and_13_out, not_21_out, not_22_out);
  not not_22 (not_22_out, s00);
  not not_23 (not_23_out, s03);
  not not_24 (not_24_out, s02);
  and and_14 (and_14_out, not_23_out, not_24_out, s01);
  not not_25 (not_25_out, s03);
  and and_15 (and_15_out, not_25_out, s01, not_26_out);
  not not_26 (not_26_out, s00);
  and and_16 (and_16_out, s02, not_27_out, s00);
  not not_27 (not_27_out, s01);
  and and_17 (and_17_out, s03, not_28_out, not_29_out);
  not not_28 (not_28_out, s02);
  not not_29 (not_29_out, s01);
  and and_18 (and_18_out, s03, s02, s00);
  not not_30 (not_30_out, s02);
  and and_19 (and_19_out, not_30_out, not_31_out);
  not not_31 (not_31_out, s01);
  not not_32 (not_32_out, s03);
  and and_20 (and_20_out, not_32_out, s02);
  not not_33 (not_33_out, s03);
  and and_21 (and_21_out, not_33_out, not_34_out, not_35_out);
  not not_34 (not_34_out, s01);
  not not_35 (not_35_out, s00);
  not not_36 (not_36_out, s02);
  and and_22 (and_22_out, s01, s00);
  and and_23 (and_23_out, s03, s01);
  not not_37 (not_37_out, s02);
  and and_24 (and_24_out, not_37_out, not_38_out);
  not not_38 (not_38_out, s00);
  not not_39 (not_39_out, s03);
  and and_25 (and_25_out, not_39_out, s01);
  not not_40 (not_40_out, s03);
  and and_26 (and_26_out, not_40_out, s02, s00);
  not not_41 (not_41_out, s02);
  and and_27 (and_27_out, s03, not_41_out, not_42_out);
  not not_42 (not_42_out, s01);
  or or_1 (g, and_1_out, and_2_out, and_3_out, and_4_out, and_5_out);
  or or_2 (f, and_6_out, and_7_out, and_8_out, and_9_out);
  or or_3 (e, and_10_out, and_11_out, and_12_out);
  or or_4 (c, and_19_out, s00, and_20_out);
  or or_5 (b, and_21_out, not_36_out, and_22_out, and_23_out);
  or or_6 (a, and_24_out, and_25_out, and_26_out, and_27_out);
  or or_7 (d, and_13_out, and_14_out, and_15_out, and_16_out, and_17_out, and_18_out);
endmodule

// x-:--
module x_____7_segDisplay (
  input  s02,
  input  s01,
  input  s00,
  output g,
  output f,
  output e,
  output d,
  output c,
  output b,
  output a
);

  wire and_1_out, and_2_out, and_3_out, and_4_out, and_5_out, and_6_out, and_7_out, and_8_out, and_9_out,
       and_10_out, and_11_out, and_12_out, and_13_out, and_14_out, and_15_out, not_1_out, not_2_out,
       not_3_out, not_4_out, not_5_out, not_6_out, not_7_out, not_8_out, not_9_out, not_10_out, not_11_out,
       not_12_out, not_13_out, not_14_out, not_15_out, not_16_out, not_17_out, not_18_out, not_19_out,
       not_20_out, not_21_out;

  or or_1 (g, s01, s02);
  not not_1 (not_1_out, s01);
  not not_2 (not_2_out, s00);
  not not_3 (not_3_out, s01);
  not not_4 (not_4_out, s00);
  not not_5 (not_5_out, s02);
  not not_6 (not_6_out, s00);
  not not_7 (not_7_out, s00);
  not not_8 (not_8_out, s02);
  not not_9 (not_9_out, s00);
  not not_10 (not_10_out, s02);
  not not_11 (not_11_out, s00);
  not not_12 (not_12_out, s01);
  not not_13 (not_13_out, s01);
  not not_14 (not_14_out, s01);
  not not_15 (not_15_out, s00);
  not not_16 (not_16_out, s02);
  not not_17 (not_17_out, s00);
  not not_18 (not_18_out, s02);
  not not_19 (not_19_out, s00);
  not not_20 (not_20_out, s01);
  and and_1 (and_1_out, not_1_out, not_2_out);
  and and_2 (and_2_out, s02, not_3_out);
  and and_3 (and_3_out, s02, not_4_out);
  and and_4 (and_4_out, not_5_out, not_6_out);
  and and_5 (and_5_out, s01, not_7_out);
  and and_6 (and_6_out, not_8_out, not_9_out);
  and and_7 (and_7_out, not_10_out, s01);
  and and_8 (and_8_out, s01, not_11_out);
  and and_9 (and_9_out, s02, not_12_out, s00);
  or or_2 (c, not_13_out, s00, s02);
  not not_21 (not_21_out, s02);
  and and_10 (and_10_out, not_14_out, not_15_out);
  and and_11 (and_11_out, s01, s00);
  and and_12 (and_12_out, not_16_out, not_17_out);
  and and_13 (and_13_out, not_18_out, s01);
  and and_14 (and_14_out, s01, not_19_out);
  and and_15 (and_15_out, s02, not_20_out, s00);
  or or_3 (f, and_1_out, and_2_out, and_3_out);
  or or_4 (e, and_4_out, and_5_out);
  or or_5 (d, and_6_out, and_7_out, and_8_out, and_9_out);
  or or_6 (b, not_21_out, and_10_out, and_11_out);
  or or_7 (a, and_12_out, and_13_out, and_14_out, and_15_out);
endmodule
